# Fritzing sketch Esquemática microSD reloj DS18B20 (saved by Fritzing 0.9.3b)
breadboards: 1

parts:
  Componente1 = Arduino Nano (Rev3.0)
  U1 = DS1307 [package=so08]
  microSD1 = MicroSD Card Module
  R1 = Resistor [tolerance=±5% resistance=4.7k package=THT]
  DS1 = DS18B20 1-Wire Temperature Sensor [part_number=DS18B20]

nets:
  GND: Componente1.GND, U1.X2, microSD1.GND, DS1.GND
  N1: Componente1.D6, U1.VBATT
  N2: Componente1.D7, U1.GND
  N3: Componente1.D8, U1.SDA
  N4: Componente1.D9, R1.Pin_0, DS1.DQ
  N5: Componente1.D10, microSD1.CS
  N6: Componente1.D11/MOSI, microSD1.MOSI
  N7: Componente1.D12/MISO, microSD1.MISO
  5V: Componente1.5V, U1.X1, microSD1.VCC, R1.Pin_1, DS1.VDD
  N8: Componente1.D13/SCK, microSD1.SCK

notes:
  DS1302
